# Fritzing sketch braille_prototype (saved by Fritzing 0.9.3b)
breadboards: 1

parts:
  Part1 = Arduino Uno (Rev3)
  Q1 = Basic FET N-Channel [package="D2Pak [SMD]"]
  R1 = Resistor [tolerance=±5% resistance=220 package=THT]
  L1 = Solenoid
  VCC1 = Battery block 9V

nets:
  N1: Part1.D9_PWM, R1.Pin_0
  N2: Part1.GND, Q1.source, VCC1.-
  N3: Q1.Gate, R1.Pin_1
  N4: Q1.drain, L1.pin1
  N5: L1.pin2, VCC1.+
